# Fritzing sketch FSR (saved by Fritzing 0.9.3b)
breadboards: 1

parts:
  Part1 = Analog Digital MUX Breakout
  Part2 = Arduino Uno (Rev3) - ICSP
  J1 = Basic Force Sensing Resistor (FSR) [package=THT]
  J2 = Basic Force Sensing Resistor (FSR) [package=THT]

nets:
  N1: Part1.C0, J1.pin_0
  N2: Part1.C1, J2.pin_0
  GND: Part1.GND, Part1.S1, Part1.S2, Part1.S3, Part2.GND
  VCC: Part1.VCC, Part1.EN, Part2.5V
  N3: Part1.S0, Part2.D12/MISO
  N4: Part1.SIG, Part2.A1

// code stored in the sketch: FSR.ino
const int fsrPin = A0; // Analog pin connected to FSR
const int threshold = 600; // Adjust this threshold based on your FSR and setup

void setup() {
  Serial.begin(9600); // Initialize serial communication
  pinMode(12, OUTPUT);
}

void loop() {
  digitalWrite(12,HIGH);
  int fsrValue = analogRead(fsrPin); // Read FSR value from analog pin

    Serial.println("FSR0:");
    Serial.print(fsrValue);
    Serial.println();
  delay(1000);
  digitalWrite(12,LOW);
  fsrValue = analogRead(fsrPin); // Read FSR value from analog pin

    Serial.println("FSR1:"); 
    Serial.print(fsrValue);
    Serial.println();
  delay(1000);
}
